# Fritzing sketch anemo (saved by Fritzing 0.9.3b)
breadboards: 1

parts:
  J1 = screw terminal, 3 pins
  HLK-PM1 = HLK-PM01
  Part1 = Adafruit ADS1115 16Bit I2C ADC [part_number="Adafruit #1085"]
  Raspberry_Pi_Zero1 = Raspberry Pi Zero

nets:
  N1: J1.pin1, HLK-PM1.AC#0
  N2: J1.pin3, HLK-PM1.AC#1
  N3: HLK-PM1.-Vo, Part1.GND
  VDD: HLK-PM1.+Vo, Part1.VDD, Raspberry_Pi_Zero1.5V

custom parts:
  Adafruit ADS1115 16Bit I2C ADC: For microcontrollers without an analog-to-digital converter or when you want a higher-precision ADC, the ADS1115 provides 16-bit precision at 860 samples/second over I2C. The chip can be configured as 4 single-ended input channels, or two differential channels. As a nice bonus, it even includes a programmable gain amplifier, up to x16, to help boost up smaller single/differential signals to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
